# Fritzing sketch schema (saved by Fritzing 0.9.3b)
breadboards: 1

parts:
  8x8_LED_Modul_mit_MAX1 = 8x8 LED Modul mit MAX7219 [package=THT]
  Componente1 = Arduino Uno (Rev3)
  U1 = POT [package=pot_mammoth]

nets:
  N1: 8x8_LED_Modul_mit_MAX1.VCC_Eingang, 8x8_LED_Modul_mit_MAX1.GND_Eingang, Componente1.GND, U1.S, U1.E
  N2: 8x8_LED_Modul_mit_MAX1.DIN_Eingang, Componente1.D12/MISO
  N3: 8x8_LED_Modul_mit_MAX1.CS_Eingang, Componente1.D10_PWM/SS
  N4: 8x8_LED_Modul_mit_MAX1.CLK_Eingang, Componente1.D11_PWM/MOSI
  N5: Componente1.A0, U1.A
